# Fritzing sketch lpf (saved by Fritzing 0.9.0b)
stripboards: 1

parts:
  R15 = Resistor [tolerance=±5% resistance=1k package=THT]
  R14 = Resistor [tolerance=±1% resistance=1k package=THT]
  C17 = Ceramic Capacitor [capacitance=47nF voltage=6.3V package="200 mil [THT, multilayer]"]
  C15 = Ceramic Capacitor [capacitance=330nF voltage=16V package="200 mil [THT, multilayer]"]
  C8 = Ceramic Capacitor [capacitance=330nF package="100 mil [THT, multilayer]"]
  C16 = Electrolytic Capacitor [capacitance=4.7µF package="100 mil [THT, electrolytic]"]
  VR5_LPF1 = Rotary Potentiometer (Large) [maximum_resistance=100kΩ package=THT]
  VR4_LPF1 = Rotary Potentiometer (Large) [maximum_resistance=100kΩ package=THT]
  IC2 = IC, DIP package, 14 pins [chip_label=TL074]
  R19 = Resistor [tolerance=±5% resistance=10k package=THT]
  R18 = Resistor [tolerance=±5% resistance=10k package=THT]
  R16 = Resistor [tolerance=±5% resistance=33k package=THT]
  R20 = Resistor [tolerance=±5% resistance=47k package=THT]
  R17 = Resistor [tolerance=±5% resistance=22k package=THT]

nets:
  N1: R15.Pin_0, C8.0, VR4_LPF1.leg2
  N2: R15.Pin_1, VR5_LPF1.leg1, VR5_LPF1.wiper
  N3: R14.Pin_0, IC2.pin1, IC2.pin2
  N4: R14.Pin_1, VR4_LPF1.leg1, VR4_LPF1.wiper
  N5: C17.0, IC2.pin10, R18.Pin_0
  N6: C17.1, C8.1, IC2.pin14, R16.Pin_0, R20.Pin_0
  Vcc2: C15.0, R20.Pin_1, R17.Pin_0
  N7: C15.1, VR5_LPF1.leg2, IC2.pin12
  N8: C16.+, IC2.pin8, R19.Pin_0
  9V/Vcc: IC2.pin4
  N9: IC2.pin9, R19.Pin_1, R18.Pin_1
  GND: IC2.pin11
  N10: IC2.pin13, R16.Pin_1, R17.Pin_1
