# Fritzing sketch rat2_blend (saved by Fritzing 0.9.0b)
circuit board: 8.46667cm x 5.64444cm
breadboards: 1

parts:
  R1 = Resistor [tolerance=±5% resistance=100 package=THT]
  R6 = Resistor [tolerance=±5% resistance=1k package=THT]
  R7 = Resistor [tolerance=±1% resistance=560 package=THT]
  R19 = Resistor [tolerance=±5% resistance=10k package=THT]
  R11 = Resistor [tolerance=±0.05% resistance=1M package=THT]
  R13 = Resistor [tolerance=±1% resistance=10k package=THT]
  R14 = Resistor [tolerance=±1% resistance=1k package=THT]
  D1 = Rectifier Diode [part_number=1N4001 package="300 mil [THT]"]
  D2 = Rectifier Diode [part_number=1N4148 package="300 mil [THT]"]
  D3 = Rectifier Diode [part_number=1N4148 package="300 mil [THT]"]
  C3 = Ceramic Capacitor [capacitance=22nF package="100 mil [THT, multilayer]"]
  C4 = Ceramic Capacitor [capacitance=1nF package="100 mil [THT, multilayer]"]
  C5 = Ceramic Capacitor [capacitance=100pF package="100 mil [THT, multilayer]"]
  C8 = Ceramic Capacitor [capacitance=330nF package="100 mil [THT, multilayer]"]
  C9 = Ceramic Capacitor [capacitance=10nF package="100 mil [THT, multilayer]"]
  C10 = Ceramic Capacitor [capacitance=33pF package="100 mil [THT, multilayer]"]
  C12 = Ceramic Capacitor [capacitance=3.3nF voltage=16V package="200 mil [THT, multilayer]"]
  C15 = Ceramic Capacitor [capacitance=330nF voltage=16V package="200 mil [THT, multilayer]"]
  C13 = Ceramic Capacitor [capacitance=22nF voltage=16V package="200 mil [THT, multilayer]"]
  C17 = Ceramic Capacitor [capacitance=47nF voltage=16V package="200 mil [THT, multilayer]"]
  C6 = Electrolytic Capacitor [capacitance=4.7µF package="100 mil [THT, electrolytic]"]
  C7 = Electrolytic Capacitor [capacitance=2.2µF package="100 mil [THT, electrolytic]"]
  C11 = Electrolytic Capacitor [capacitance=4.7µF package="100 mil [THT, electrolytic]"]
  C14 = Electrolytic Capacitor [capacitance=1µF package="100 mil [THT, electrolytic]"]
  C16 = Electrolytic Capacitor [capacitance=4.7µF package="100 mil [THT, electrolytic]"]
  IC2 = IC, DIP package, 8 pins [chip_label=LM308]
  R3 = Resistor [tolerance=±5% resistance=100k package=THT]
  R4 = Resistor [tolerance=±5% resistance=2.2M package=THT]
  R5 = Resistor [tolerance=±5% resistance=2.2M package=THT]
  R8 = Resistor [tolerance=±5% resistance=47 package=THT]
  R9 = Resistor [tolerance=±5% resistance=1k package=THT]
  R10 = Resistor [tolerance=±5% resistance=1.5k package=THT]
  R12 = Resistor [tolerance=±5% resistance=10k package=THT]
  R15 = Resistor [tolerance=±5% resistance=1k package=THT]
  R16 = Resistor [tolerance=±5% resistance=15k package=THT]
  R17 = Resistor [tolerance=±5% resistance=10k package=THT]
  R18 = Resistor [tolerance=±5% resistance=10k package=THT]
  R20 = Resistor [tolerance=±5% resistance=50k package=THT]
  C1 = Electrolytic Capacitor [capacitance=100µF voltage=50V package="100 mil [THT, electrolytic]"]
  Q1 = 2N7000 FET N-Channel [part_number=2N5458 package=TO92]
  OUT = Audio Jack (TRS) 3.5mm [package="4Ucon 08780 [THT]"]
  IN = Audio Jack (TRS) 3.5mm [package="PG203J [THT]"]
  IC1 = IC, DIP package, 14 pins [chip_label=TL074]
  Power_plug1 = Power plug
  R2 = Resistor [tolerance=±1% resistance=100k package=THT]
  VR1_DRIVE = Rotary Potentiometer (Large) [maximum_resistance=100kΩ package=THT]
  VR4_LPF = Rotary Potentiometer (Large) [maximum_resistance=100kΩ package=THT]
  VR3_VOUT = Rotary Potentiometer (Large) [maximum_resistance=100kΩ package=THT]
  VR2_FILTER = Rotary Potentiometer (Large) [maximum_resistance=100kΩ package=THT]
  VR5_LPF = Rotary Potentiometer (Large) [maximum_resistance=100kΩ package=THT]
  C2 = Electrolytic Capacitor [capacitance=47µF voltage=50V package="100 mil [THT, electrolytic]"]
  VR6_BLE = Rotary Potentiometer (Large) [maximum_resistance=100kΩ package=THT]

nets:
  9V/Vcc: R1.Pin_0, D1.cathode, C9.0, C14.+, IC2.pin7, R12.Pin_0, C1.+, Q1.drain, Q1.source, IC1.pin4, R2.Pin_0
  N1: R1.Pin_1, Power_plug1.VCC
  N2: R6.Pin_0, C3.1, R5.Pin_1, IC1.pin3
  N3: R6.Pin_1, C4.1, IC2.pin3
  N4: R7.Pin_0, C5.0, IC2.pin2, R8.Pin_0, VR1_DRIVE.leg2
  N5: R7.Pin_1, C6.+
  N6: R19.Pin_0, C16.+, IC1.pin8
  N7: R19.Pin_1, R18.Pin_1, IC1.pin9
  N8: R11.Pin_0, C13.0, Q1.gate
  GND: R11.Pin_1, R13.Pin_1, D1.anode, D2.anode, D3.cathode, C4.0, C9.1, C12.0, C6.-, C7.-, IC2.pin4, R3.Pin_1, R4.Pin_1, R12.Pin_1, C1.-, OUT.Sleeve, IN.Sleeve, IC1.pin11, Power_plug1.GND, VR3_VOUT.leg1, C2.-
  N9: R13.Pin_0, C14.-, VR6_BLE.leg1
  N10: R14.Pin_0, IC1.pin1, IC1.pin2
  N11: R14.Pin_1, VR4_LPF.leg1, VR4_LPF.wiper
  N12: D2.cathode, D3.anode, C11.-, VR2_FILTER.leg2
  N13: C3.0, R4.Pin_0, IN.Tip
  N14: C5.1, IC2.pin6, R9.Pin_1, VR1_DRIVE.leg1, VR1_DRIVE.wiper
  N15: C8.0, R15.Pin_0, VR4_LPF.leg2
  N16: C8.1, C17.1, R16.Pin_0, R20.Pin_0, IC1.pin14
  N17: C10.0, IC2.pin1
  N18: C10.1, IC2.pin8
  N19: C12.1, C13.1, R10.Pin_0
  4.5V/Vcc2: C15.0, R3.Pin_0, R5.Pin_0, R17.Pin_0, R20.Pin_1, R2.Pin_1, C2.+
  N20: C15.1, IC1.pin12, VR5_LPF.leg2
  N21: C17.0, R18.Pin_0, IC1.pin10
  N22: C7.+, R8.Pin_1
  N23: C11.+, R9.Pin_0
  N24: C16.-, VR6_BLE.leg2
  N25: R10.Pin_1, VR2_FILTER.leg1, VR2_FILTER.wiper
  N26: R15.Pin_1, VR5_LPF.leg1, VR5_LPF.wiper
  N27: R16.Pin_1, R17.Pin_1, IC1.pin13
  N28: OUT.Tip, VR3_VOUT.wiper
  N29: VR3_VOUT.leg2, VR6_BLE.wiper

custom parts:
  2N7000 FET N-Channel: A 2N7000 MOSFET N-Channel Transistor
